// Logisim project ALU.circ as structural Verilog: 1 circuit, main circuit ALU
module ALU (
  input  [31:0] A,
  input  [31:0] B,
  input  [4:0] Shift,
  input  [3:0] Codop,
  input  CarryIn,
  output [31:0] S,
  output [3:0] Flags
);

  wire ADC_V, ASR_C, BORROW_CMP_OUT, BORROW_OUT, CARRY_CMN_OUT, CARRY_OUT, CMN_V, CMP_V, LSL_C, not_3_out,
       SBC_V, subtractor_2_bout, subtractor_3_bout, xnor_1_out, xnor_2_out, xor_1_out, xor_2_out, xor_3_out,
       xor_4_out, xor_5_out, xor_6_out;
  wire [4:0] negator_1_out, subtractor_1_out;
  wire [31:0] ADC_OUT, AND_OUT, ASR_OUT, BIC_OUT, CARRY_MUL_OUT, CMN_OUT, CMP_OUT, EOR_OUT, LSL_OUT, LSR_OUT,
       MUL_OUT, multiplexer_3_out, MVN_OUT, not_1_out, ORR_OUT, ROR_OUT, RSB_OUT, SBC_OUT;

  Shifter #(.width(32)) shifter_1 (.in(B), .\dist (Shift), .out(LSL_OUT));
  Shifter #(.shift("lr"), .width(32)) shifter_2 (.in(B), .\dist (Shift), .out(LSR_OUT));
  Shifter #(.shift("ar"), .width(32)) shifter_3 (.in(B), .\dist (Shift), .out(ASR_OUT));
  Shifter #(.shift("rr"), .width(32)) shifter_4 (.in(B), .\dist (Shift), .out(ROR_OUT));
  xor xor_1 (xor_1_out, B[31], CMN_OUT[31]);
  xor xor_2 (xor_2_out, A[31], B[31]);
  BitSelector #(.width(32)) bitselector_1 (.in(B), .out(LSL_C), .sel(negator_1_out));
  Negator #(.width(5)) negator_1 (.in(Shift), .out(negator_1_out));
  BitSelector #(.width(32)) bitselector_2 (.in(B), .out(ASR_C), .sel(subtractor_1_out));
  Subtractor #(.width(5)) subtractor_1 (.a(Shift), .b(5'b00001), .out(subtractor_1_out));  // open: bin, bout
  assign not_1_out = ~A;  // NOT_Gate not_1, 32 bits wide
  xor xor_3 (xor_3_out, B[31], ADC_OUT[31]);
  and and_1 (ADC_V, xor_3_out, xnor_1_out);
  xnor xnor_1 (xnor_1_out, A[31], B[31]);
  xor xor_4 (xor_4_out, B[31], ADC_OUT[31]);
  and and_2 (SBC_V, xor_4_out, xor_5_out);
  xor xor_5 (xor_5_out, A[31], ADC_OUT[31]);
  and and_3 (CMP_V, xor_1_out, xor_2_out);
  xor xor_6 (xor_6_out, B[31], CMN_OUT[31]);
  and and_4 (CMN_V, xor_6_out, xnor_2_out);
  xnor xnor_2 (xnor_2_out, A[31], B[31]);
  assign AND_OUT = A & B;  // AND_Gate and_5, 32 bits wide
  assign EOR_OUT = A ^ B;  // XOR_Gate xor_7, 32 bits wide
  assign MVN_OUT = ~A;  // NOT_Gate not_2, 32 bits wide
  assign BIC_OUT = not_1_out & B;  // AND_Gate and_6, 32 bits wide
  assign ORR_OUT = A | B;  // OR_Gate or_1, 32 bits wide
  Multiplexer #(.enable("false"), .select(4), .width(32)) multiplexer_1 (
    .in0(AND_OUT), .in1(EOR_OUT), .in2(LSL_OUT), .in3(LSR_OUT), .in4(ASR_OUT), .in5(ADC_OUT), .in6(SBC_OUT),
    .in7(ROR_OUT), .in8(B), .in9(RSB_OUT), .in10(B), .in11(B), .in12(ORR_OUT), .in13(MUL_OUT),
    .in14(BIC_OUT), .in15(MVN_OUT), .out(S), .sel(Codop));
  not not_3 (not_3_out, CarryIn);
  not not_4 (BORROW_OUT, subtractor_2_bout);
  not not_5 (BORROW_CMP_OUT, subtractor_3_bout);
  Adder #(.width(32)) adder_1 (.a(A), .b(B), .out(ADC_OUT), .cin(CarryIn), .cout(CARRY_OUT));
  Subtractor #(.width(32)) subtractor_2 (.a(B), .b(A), .out(SBC_OUT), .bin(not_3_out), .bout(subtractor_2_bout));
  Multiplier #(.width(32)) multiplier_1 (.a(B), .b(A), .out(MUL_OUT), .cout(CARRY_MUL_OUT));  // open: cin
  Negator #(.width(32)) negator_2 (.in(A), .out(RSB_OUT));
  Adder #(.width(32)) adder_2 (.a(A), .b(B), .out(CMN_OUT), .cout(CARRY_CMN_OUT));  // open: cin
  Subtractor #(.width(32)) subtractor_3 (.a(B), .b(A), .out(CMP_OUT), .bout(subtractor_3_bout));  // open: bin
  Multiplexer #(.enable("false"), .select(4)) multiplexer_2 (
    .in0(1'b0), .in1(1'b0), .in2(1'b0), .in3(1'b0), .in4(1'b0), .in5(ADC_V), .in6(SBC_V), .in7(1'b0),
    .in8(1'b0), .in9(1'b0), .in10(CMP_V), .in11(CMN_V), .in12(1'b0), .in13(1'b0), .in14(1'b0), .in15(1'b0),
    .out(Flags[0]), .sel(Codop));
  Multiplexer #(.enable("false"), .select(4), .width(32)) multiplexer_3 (
    .in0(AND_OUT), .in1(EOR_OUT), .in2(LSL_OUT), .in3(LSR_OUT), .in4(ASR_OUT), .in5(ADC_OUT), .in6(SBC_OUT),
    .in7(ROR_OUT), .in8(AND_OUT), .in9(RSB_OUT), .in10(CMP_OUT), .in11(CMN_OUT), .in12(ORR_OUT),
    .in13(MUL_OUT), .in14(BIC_OUT), .in15(MVN_OUT), .out(multiplexer_3_out), .sel(Codop));
  Comparator #(.width(32)) comparator_1 (
    .a(multiplexer_3_out), .b({32{1'b0}}), .eq(Flags[2]), .lt(Flags[3]));  // open: gt
  Multiplexer #(.enable("false"), .select(4)) multiplexer_4 (
    .in0(1'b0), .in1(1'b0), .in2(LSL_C), .in3(ASR_C), .in4(ASR_C), .in5(CARRY_OUT), .in6(BORROW_OUT),
    .in7(ROR_OUT[31]), .in8(1'b0), .in9(1'b0), .in10(BORROW_CMP_OUT), .in11(CARRY_CMN_OUT), .in12(1'b0),
    .in13(1'b0), .in14(1'b0), .in15(1'b0), .out(Flags[1]), .sel(Codop));

  // Other names for the same wires on the sheet: A_IN[31:0] = A; B_IN[31:0] = B; CARRY_IN = CarryIn;
  //   CODEOP_IN[3:0] = Codop; V_OUT = Flags[0]; C_OUT = Flags[1]; Z_OUT = Flags[2]; N_OUT = Flags[3]; LSR_C = ASR_C;
  //   MAIN_MUX_OUT[31:0] = S; SHIFT_IN[4:0] = Shift

  // Notes on the sheet:
  //   Note: for ROR, C = N
  //   Note 2: assume that shift > 0 for LSL and LSR
  //   Shifters
  //   Gates
  //   Arithmetic
  //   Flags
  //   FLAG C
  //   FLAG V
  //   Outputs
  //   FLAG N & Z
endmodule
