// Logisim project BancDeRegistres.circ as structural Verilog: 1 circuit, main circuit BancRegistre
module BancRegistre (
  input  [31:0] DataIn,
  input  [2:0] RegDest,
  input  [2:0] RegA,
  input  [2:0] RegB,
  input  Clk,
  input  Reset,
  output [31:0] AOut,
  output [31:0] BOut,
  output [31:0] R0,
  output [31:0] R1,
  output [31:0] R2,
  output [31:0] R3,
  output [31:0] R4,
  output [31:0] R5,
  output [31:0] R6,
  output [31:0] R7
);

  wire WE0, WE1, WE2, WE3, WE4, WE5, WE6, WE7;

  Register #(.width(32)) register_1 (.D(DataIn), .en(WE0), .clk(Clk), .Q(R0));  // open: clr
  Register #(.width(32)) register_2 (.D(DataIn), .en(WE1), .clk(Clk), .Q(R1));  // open: clr
  Register #(.width(32)) register_3 (.D(DataIn), .en(WE2), .clk(Clk), .Q(R2));  // open: clr
  Register #(.width(32)) register_4 (.D(DataIn), .en(WE3), .clk(Clk), .Q(R3));  // open: clr
  Demultiplexer #(.enable("false"), .select(3)) demultiplexer_1 (
    .out0(WE0), .out1(WE1), .out2(WE2), .out3(WE3), .out4(WE4), .out5(WE5), .out6(WE6), .out7(WE7),
    .in(1'b1), .sel(RegDest));
  Register #(.width(32)) register_5 (.D(DataIn), .en(WE4), .clk(Clk), .Q(R4));  // open: clr
  Register #(.width(32)) register_6 (.D(DataIn), .en(WE5), .clk(Clk), .Q(R5));  // open: clr
  Register #(.width(32)) register_7 (.D(DataIn), .en(WE6), .clk(Clk), .Q(R6));  // open: clr
  Register #(.width(32)) register_8 (.D(DataIn), .en(WE7), .clk(Clk), .Q(R7));  // open: clr
  Multiplexer #(.enable("false"), .select(3), .width(32)) multiplexer_1 (
    .in0(R0), .in1(R1), .in2(R2), .in3(R3), .in4(R4), .in5(R5), .in6(R6), .in7(R7), .out(AOut), .sel(RegA));
  Multiplexer #(.enable("false"), .select(3), .width(32)) multiplexer_2 (
    .in0(R0), .in1(R1), .in2(R2), .in3(R3), .in4(R4), .in5(R5), .in6(R6), .in7(R7), .out(BOut), .sel(RegB));

  // Other names for the same wires on the sheet: A_OUT[31:0] = AOut; B_OUT[31:0] = BOut; DIN[31:0] = DataIn;
  //   REG_A_IN[2:0] = RegA; REG_B_IN[2:0] = RegB; REG_DEST_IN[2:0] = RegDest; RST = Reset
endmodule
