// Logisim project Ctl_Conditional.circ as structural Verilog: 1 circuit, main circuit Conditional
module Conditional (
  input  Enable,
  input  [15:0] Instruction,
  input  Z,
  input  C,
  input  N,
  input  V,
  output [10:0] Offset,
  output Verified
);

  wire multiplexer_2_out, not_1_out, not_2_out, not_3_out, not_4_out, not_5_out, not_6_out, not_7_out,
       or_1_out, or_2_out, or_3_out, xor_1_out;
  wire [10:0] bit_extender_1_out, multiplexer_1_out;

  not not_1 (not_1_out, Z);
  not not_2 (not_2_out, C);
  not not_3 (not_3_out, N);
  not not_4 (not_4_out, V);
  or or_1 (or_1_out, Z, ~C);  // OR_Gate
  xor xor_1 (xor_1_out, N, V);
  Bit_Extender #(.out_width(11), .\type ("input")) bit_extender_1 (
    .in(Instruction[7:0]), .out(bit_extender_1_out));  // open: extend
  not not_5 (not_5_out, or_1_out);
  not not_6 (not_6_out, xor_1_out);
  not not_7 (not_7_out, or_2_out);
  or or_2 (or_2_out, Z, xor_1_out);
  Multiplexer #(.enable("false"), .width(11)) multiplexer_1 (
    .in0(bit_extender_1_out), .in1(Instruction[10:0]), .out(multiplexer_1_out), .sel(Instruction[13]));
  Multiplexer #(.enable("false"), .select(4)) multiplexer_2 (
    .in0(Z), .in1(not_1_out), .in2(C), .in3(not_2_out), .in4(N), .in5(not_3_out), .in6(V), .in7(not_4_out),
    .in8(not_5_out), .in9(or_1_out), .in10(not_6_out), .in11(xor_1_out), .in12(not_7_out), .in13(or_2_out),
    .in14(1'b1), .out(multiplexer_2_out), .sel(Instruction[11:8]));  // open: in15
  assign Offset = Enable ? multiplexer_1_out : 11'bz;  // Controlled_Buffer controlled_buffer_1
  or or_3 (or_3_out, Instruction[13], multiplexer_2_out);
  Pull_Resistor pull_resistor_1 (.node(Offset));
  Pull_Resistor pull_resistor_2 (.node(Verified));
  assign Verified = Enable ? or_3_out : 1'bz;  // Controlled_Buffer controlled_buffer_2

  // Other names for the same wires on the sheet: INS[15:0] = Instruction; CODE[3:0] = Instruction[11:8];
  //   COND = Instruction[13]

  // Notes on the sheet:
  //   Verification
  //   Offset
endmodule
