// Logisim project Ctl_Opcode_Decoder.circ as structural Verilog: 1 circuit, main circuit Opcode_Decoder
module Opcode_Decoder (
  input  [5:0] Opcode,
  output Shift,
  output Data_Processing,
  output Load_Store,
  output SP_Address,
  output Conditional
);

  wire and_1_out, and_3_out, and_5_out, and_7_out, and_8_out, and_9_out, nand_2_out, nand_3_out, nand_4_out,
       not_1_out, not_2_out;

  nand nand_1 (Shift, Opcode[0], Opcode[1]);
  nand nand_2 (nand_2_out, Opcode[4], Opcode[3]);
  nand nand_3 (nand_3_out, Opcode[2], Opcode[0]);
  and and_1 (and_1_out, nand_2_out, nand_3_out);
  and and_2 (Data_Processing, and_1_out, Opcode[1]);
  and and_3 (and_3_out, Opcode[0], Opcode[3]);
  nand nand_4 (nand_4_out, Opcode[1], Opcode[2]);
  and and_4 (Load_Store, nand_4_out, and_3_out);
  not not_1 (not_1_out, Opcode[1]);
  and and_5 (and_5_out, Opcode[0], not_1_out);
  and and_6 (SP_Address, and_5_out, and_7_out);
  and and_7 (and_7_out, Opcode[2], Opcode[3]);
  and and_8 (and_8_out, Opcode[0], Opcode[1]);
  not not_2 (not_2_out, Opcode[2]);
  and and_9 (and_9_out, not_2_out, Opcode[3]);
  and and_10 (Conditional, and_8_out, and_9_out);

  // Other names for the same wires on the sheet: COND = Conditional; DP = Data_Processing; LS = Load_Store;
  //   OP_IN[5:0] = Opcode; SP = SP_Address

  // Notes on the sheet:
  //   Shift, add, sub, mov (00XXXX)
  //   Load/Store (1001XX)
  //   SP Address (1011XX)
  //   Data Processing (01000X)
  //   Conditional branch (1101 cond)(11100 uncond)
endmodule
